// Logisim project cuptor.circ as structural Verilog
module main (
  input  RESET,
  output [7:0] TEMP,
  output [2:0] T5,
  output [4:0] T30,
  output [2:0] TEMP_SELECTION
);

  wire CLK_out, cuptor_1_ck, cuptor_1_insertfood, cuptor_1_preheating, START_out, TEMP_DOWN_out, TEMP_UP_out;
  wire [3:0] binary_to_decimal_converter_1_decimal, binary_to_decimal_converter_1_unit;
  wire [6:0] hex2_7seg_1_a_b_c_d_e_f_g, hex2_7seg_2_a_b_c_d_e_f_g, hex2_7seg_3_a_b_c_d_e_f_g;

  Clock CLK (.out(CLK_out));
  Button TEMP_UP (.out(TEMP_UP_out));
  Button TEMP_DOWN (.out(TEMP_DOWN_out));
  Button START (.out(START_out));
  Temperature_Selector temperature_selector_1 (
    .clk(CLK_out), .rst(RESET), .up(TEMP_UP_out), .down(TEMP_DOWN_out), .temp(TEMP),
    .temp_Selection(TEMP_SELECTION));
  Cuptor cuptor_1 (
    .clk(CLK_out), .rst(RESET), .start(START_out), .sel(TEMP_SELECTION), .preheating(cuptor_1_preheating),
    .insertFood(cuptor_1_insertfood), .ck(cuptor_1_ck), .counter5_out(T5), .counter30_out(T30));
  LED PH (.in(cuptor_1_preheating));
  LED FI (.in(cuptor_1_insertfood));
  LED CK (.in(cuptor_1_ck));
  _7_Segment_Display #(.active("false"), .decimalPoint("false")) u_7_segment_display_1 (
    .g(hex2_7seg_1_a_b_c_d_e_f_g[0]), .f(hex2_7seg_1_a_b_c_d_e_f_g[1]), .a(hex2_7seg_1_a_b_c_d_e_f_g[6]),
    .b(hex2_7seg_1_a_b_c_d_e_f_g[5]), .e(hex2_7seg_1_a_b_c_d_e_f_g[2]), .d(hex2_7seg_1_a_b_c_d_e_f_g[3]),
    .c(hex2_7seg_1_a_b_c_d_e_f_g[4]));
  Binary_to_decimal_converter binary_to_decimal_converter_1 (
    .Bin_num({3'b000, T30}), .Unit(binary_to_decimal_converter_1_unit),
    .Decimal(binary_to_decimal_converter_1_decimal));
  hex2_7seg hex2_7seg_1 (.hex_in({1'b0, T5}), .a_b_c_d_e_f_g(hex2_7seg_1_a_b_c_d_e_f_g));
  hex2_7seg hex2_7seg_2 (.hex_in(binary_to_decimal_converter_1_unit), .a_b_c_d_e_f_g(hex2_7seg_2_a_b_c_d_e_f_g));
  _7_Segment_Display #(.active("false"), .decimalPoint("false")) u_7_segment_display_2 (
    .g(hex2_7seg_3_a_b_c_d_e_f_g[0]), .f(hex2_7seg_3_a_b_c_d_e_f_g[1]), .a(hex2_7seg_3_a_b_c_d_e_f_g[6]),
    .b(hex2_7seg_3_a_b_c_d_e_f_g[5]), .e(hex2_7seg_3_a_b_c_d_e_f_g[2]), .d(hex2_7seg_3_a_b_c_d_e_f_g[3]),
    .c(hex2_7seg_3_a_b_c_d_e_f_g[4]));
  _7_Segment_Display #(.active("false"), .decimalPoint("false")) u_7_segment_display_3 (
    .g(hex2_7seg_2_a_b_c_d_e_f_g[0]), .f(hex2_7seg_2_a_b_c_d_e_f_g[1]), .a(hex2_7seg_2_a_b_c_d_e_f_g[6]),
    .b(hex2_7seg_2_a_b_c_d_e_f_g[5]), .e(hex2_7seg_2_a_b_c_d_e_f_g[2]), .d(hex2_7seg_2_a_b_c_d_e_f_g[3]),
    .c(hex2_7seg_2_a_b_c_d_e_f_g[4]));
  hex2_7seg hex2_7seg_3 (.hex_in(binary_to_decimal_converter_1_decimal), .a_b_c_d_e_f_g(hex2_7seg_3_a_b_c_d_e_f_g));
endmodule

// VHDL entity Temperature_Selector, as the project stores it:
library IEEE;
use IEEE.STD_LOGIC_1164.ALL;
use IEEE.NUMERIC_STD.ALL;
use IEEE.std_logic_unsigned.all;

entity Temperature_Selector is
    Port ( clk : in  STD_LOGIC;
           rst : in  STD_LOGIC;
           up  : in  STD_LOGIC;
           down : in  STD_LOGIC;
           temp : out STD_LOGIC_VECTOR(7 downto 0);
           temp_Selection : out STD_LOGIC_VECTOR(2 downto 0)
         );
end Temperature_Selector;

architecture Behavioral of Temperature_Selector is
begin

    process(clk, rst, up, down)
        variable counter : std_logic_vector(2 downto 0) := "000";
        variable temp_sel : std_logic_vector(7 downto 0) := "01100100";
    begin
        if rst = '1' then
            counter := "000";
            temp_sel := "01100100";
        elsif rising_edge(clk) then
            if up = '1' then 
                counter := counter + 1;
            elsif down = '1' then
                counter := counter - 1;
            end if;

            case counter is
                when "000" =>
                    temp_sel := "01100100"; -- temperature 100
                when "001" =>
                    temp_sel := "01110011"; -- temperature 115
                when "010" =>
                    temp_sel := "10000010"; -- temperature 130
                when "011" =>
                    temp_sel := "10010001"; -- temperature 145
                when "100" =>
                    temp_sel := "10100000"; -- temperature 160
                when "101" =>
                    temp_sel := "10101111"; -- temperature 175
                when "110" =>
                    temp_sel := "10110110"; -- temperature 190
                when "111" =>
                    temp_sel := "10111100"; -- temperature 200
                when others =>
                    temp_sel := "01100100"; -- default value
            end case;
        end if;

        temp <= temp_sel;
        temp_Selection <= counter;
    end process;

end Behavioral;

// VHDL entity Cuptor, as the project stores it:
library IEEE;
use IEEE.STD_LOGIC_1164.ALL;
use IEEE.NUMERIC_STD.ALL;
use ieee.std_logic_arith.all;
use ieee.std_logic_unsigned.all;

entity Cuptor is
    Port (
        clk          : in  STD_LOGIC;
        rst          : in  STD_LOGIC;
        start        : in  STD_LOGIC;
        sel          : in  STD_LOGIC_VECTOR(2 downto 0);
        preheating   : out STD_LOGIC;
        insertFood   : out STD_LOGIC;
        ck           : out STD_LOGIC;
        counter5_out : out STD_LOGIC_VECTOR(2 downto 0);
        counter30_out: out STD_LOGIC_VECTOR(4 downto 0)
    );
end Cuptor;

architecture Behavioral of Cuptor is
    type state_type is (IDLE, PRE_HEATING, INSERT_FOOD, COOKING);
    signal state, next_state : state_type;
    signal max_count : std_logic_vector(3 downto 0) := "0101";
    signal counter5 : std_logic_vector(2 downto 0) := "101";
    signal counter30 : std_logic_vector(4 downto 0) := "11110";
    signal cook : std_logic := '0';
    signal donePreheat : std_logic := '0';
    signal counterPreheat : std_logic_vector(3 downto 0) := "0000";
begin

    -- Next state logic
    NEXT_STATE_LOGIC: process(state, start, counter30, counter5, donePreheat, sel)
    begin
        next_state <= state;
        case state is
            when IDLE =>
                if start = '1' then
                    next_state <= PRE_HEATING;
                end if;
            when PRE_HEATING =>
                if donePreheat = '1' then
                    next_state <= INSERT_FOOD;
                end if;
            when INSERT_FOOD =>
                if start = '1' then
                    next_state <= COOKING;
                elsif counter5 = "000" then
                    next_state <= IDLE;
                end if;
            when COOKING =>
                if counter30 = "00000" then
                    next_state <= IDLE;
                end if;
        end case;
    end process;

    -- Output logic for each state
    OUTPUT_LOGIC: process(clk, rst)
    begin

        if rst = '1' then
            state <= IDLE;
            counter5 <= "101";
            counter30 <= "11110";
            max_count <= "0101";
            cook <= '0';
            preheating <= '0';
            insertFood <= '0';
            counterPreheat <= "0000";
            donePreheat <= '0';
        elsif rising_edge(clk) then
            state <= next_state;
            case state is
                when IDLE =>
                    preheating <= '0';
                    insertFood <= '0';
                    cook <= '0';
                    counter5 <= "101";
                    counter30 <= "11110";
                    donePreheat <= '0';

	                case sel is
		                when "000" =>
		                    max_count <= "0101"; -- 5 seconds
		                when "001" =>
		                    max_count <= "0110"; -- 6 seconds
		                when "010" =>
		                    max_count <= "0111"; -- 7 seconds
		                when "011" =>
		                    max_count <= "1000"; -- 8 seconds
		                when "100" =>
		                    max_count <= "1001"; -- 9 seconds
		                when "101" =>
		                    max_count <= "1010"; -- 10 seconds
		                when "110" =>
		                    max_count <= "1011"; -- 11 seconds
		                when "111" =>
		                    max_count <= "1100"; -- 12 seconds
		                when others =>
		                    max_count <= "0101"; -- 5 seconds
	                end case;
                    
                when PRE_HEATING =>
                    preheating <= '1';
                    insertFood <= '0';
                    if counterPreheat = max_count then
                        donePreheat <= '1';
                        counterPreheat <= "0000";
                    else
                        counterPreheat <= counterPreheat + 1;
                    end if;
                    
                when INSERT_FOOD =>
                    donePreheat <= '0';
                    preheating <= '0';
                    insertFood <= '1';
                    if counter5 /= "000" then
                        counter5 <= counter5 - 1;
                    end if;
                    
                when COOKING =>
                    preheating <= '0';
                    insertFood <= '0';
                    cook <= '1';
                    if counter30 /= "00000" then
                        counter30 <= counter30 - 1;
                    end if;
            end case;
        end if;
    end process;

    counter5_out <= counter5;
    counter30_out <= counter30;
    ck <= cook;
end Behavioral;

// VHDL entity Binary_to_decimal_converter, as the project stores it:
LIBRARY ieee;
USE ieee.std_logic_1164.all;
USE ieee.std_logic_unsigned.all;
USE ieee.std_logic_arith.all;

ENTITY Binary_to_decimal_converter IS
  PORT (
 Bin_num: in std_logic_vector(7 downto 0);
  		Unit: out std_logic_vector(3 downto 0);
  		Decimal: out std_logic_vector(3 downto 0)  
    );
END Binary_to_decimal_converter;

ARCHITECTURE comport OF Binary_to_decimal_converter IS

signal num_int: integer:=0;
signal u,z: integer:=0;
BEGIN

	num_int<=conv_integer(bin_num);
	z<=num_int / 10;
	u<=num_int rem 10;
	process(u)
	begin
		case u is
		when 0 => unit <= x"0";
		when 1 => unit <= x"1";
		when 2 => unit <= x"2";
		when 3 => unit <= x"3";
		when 4 => unit <= x"4";
		when 5 => unit <= x"5";
		when 6 => unit <= x"6";
		when 7 => unit <= x"7";
		when 8 => unit <= x"8";
		when 9 => unit <= x"9";
		when others => unit <=x"f";
		end case;
	end process;
	process(z)
	begin
		case z is
		when 0 => Decimal <= x"0";
		when 1 => Decimal <= x"1";
		when 2 => Decimal <= x"2";
		when 3 => Decimal <= x"3";
		when 4 => Decimal <= x"4";
		when 5 => Decimal <= x"5";
		when 6 => Decimal <= x"6";
		when 7 => Decimal <= x"7";
		when 8 => Decimal <= x"8";
		when 9 => Decimal <= x"9";
		when others => Decimal <=x"f";
		end case;
	end process;
		 

	
END comport;

// VHDL entity CuptorVechi, as the project stores it:
library IEEE;
use IEEE.STD_LOGIC_1164.ALL;
use IEEE.NUMERIC_STD.ALL;
use IEEE.std_logic_arith.all;
use IEEE.std_logic_unsigned.all;

entity CuptorVechi is
    Port ( clk : in  STD_LOGIC;
           rst : in  STD_LOGIC;
           start: in STD_LOGIC;
           sel : in  STD_LOGIC_VECTOR(2 downto 0);
           preheating: out STD_LOGIC;
           insertFood: out STD_LOGIC;
           ck: out STD_LOGIC;
           counter5_out: out STD_LOGIC_VECTOR(2 downto 0); 
           counter30_out: out STD_LOGIC_VECTOR(4 downto 0)

         );
end CuptorVechi;

architecture Behavioral of CuptorVechi is
    signal max_count : std_logic_vector(3 downto 0);
    signal counter: std_logic_vector(3 downto 0) := "0000";
    signal enableCounter5 : std_logic := '0';
    signal counter5: std_logic_vector(2 downto 0) := "101";
    signal cooking: std_logic := '0';
begin

    SELECT_HEATING_TIME: process(sel)
    begin 
        case sel is
            when "000" =>
                max_count <= "0101"; -- 5 seconds
            when "001" =>
                max_count <= "0110"; -- 6 seconds
            when "010" =>
                max_count <= "0111"; -- 7 seconds
            when "011" =>
                max_count <= "1000"; -- 8 seconds
            when "100" =>
                max_count <= "1001"; -- 9 seconds
            when "101" =>
                max_count <= "1010"; -- 10 seconds
            when "110" =>
                max_count <= "1011"; -- 11 seconds
            when "111" =>
                max_count <= "1100"; -- 12 seconds
            when others =>
                max_count <= "0101"; -- 5 seconds
        end case;
    end process;

    PRE_HEATING: process(clk, rst, start)
    variable enable : std_logic := '0';
    variable counter5_var: std_logic_vector(2 downto 0) := "000";
    variable counter30_var: std_logic_vector(4 downto 0) := "00000";
    begin
    	   -- Preheating timer start 
        if (start = '1' and enableCounter5 = '0' and cooking = '0') then 
            enable := '1';
            preheating <= '1';
        elsif (rst = '1' )then 
            enable := '0';
            counter <= "0000";
            preheating <= '0';
            insertFood <= '0';
            cooking <= '0';
            enableCounter5 <= '0';
        end if;

        -- Preheating timer
        if rising_edge(clk) and enable = '1' then 
            if counter = max_count then 
                preheating <= '0';
                insertFood <= '1';
                enableCounter5 <= '1';
                enable := '0';
                counter5_var := "100"; 
            else 
                counter <= counter + 1;
            end if;
        end if;

        -- Inserting food timer logic
        if rising_edge(clk) and enableCounter5 = '1' then 
            if counter5_var = "000" then 
	            enable := '0';
	            counter <= "0000";
	            preheating <= '0';
	            insertFood <= '0';
	            cooking <= '0';
	            enableCounter5 <= '0';
            else 
                counter5_var := counter5_var - 1;
            end if;
        end if;

        -- Inserting food button pressed logic
        if rising_edge(clk) and start = '1' and enableCounter5 = '1' then
	       enable := '0';
	       counter <= "0000";
            preheating <= '0';
	       insertFood <= '0';
	       cooking <= '0';
	       enableCounter5 <= '0';
            cooking <= '1';
            counter30_var := "11110";
        end if;


	   -- Cooking logic 
        if rising_edge(clk) and cooking = '1' then 
		  if counter30_var = "00000" then 
	            enable := '0';
	            counter <= "0000";
	            preheating <= '0';
	            insertFood <= '0';
	            cooking <= '0';
	            enableCounter5 <= '0';
            else 
                counter30_var := counter30_var - 1;
            end if;
        end if;
        
       counter5 <= counter5_var;
       counter5_out <= counter5;
       counter30_out <= counter30_var;

	end process;
	ck <= cooking; 
end Behavioral;

// VHDL entity hex2_7seg, as the project stores it:
LIBRARY ieee;
USE ieee.std_logic_1164.all;

ENTITY hex2_7seg IS
  PORT (
  	hex_in : in std_logic_vector(3 downto 0);
  	a_b_c_d_e_f_g : out std_logic_vector(6 downto 0)
    );
END hex2_7seg;

--------------------------------------------------------------------------------
--Complete your VHDL description below
--------------------------------------------------------------------------------

ARCHITECTURE TypeArchitecture OF hex2_7seg IS

BEGIN

a_b_c_d_e_f_g <=   "0000001" when hex_in = x"0" else
                   "1001111" when hex_in = x"1" else
                   "0010010" when hex_in = x"2" else
                   "0000110" when hex_in = x"3" else
                   "1001100" when hex_in = x"4" else
                   "0100100" when hex_in = x"5" else
                   "0100000" when hex_in = x"6" else
                   "0001111" when hex_in = x"7" else
                   "0000000" when hex_in = x"8" else
                   "0000100" when hex_in = x"9" else
                   "0001000" when hex_in = x"A" else
                   "1100000" when hex_in = x"B" else
                   "0110000" when hex_in = x"C" else
                   "1000010" when hex_in = x"D" else 
                   "0110000" when hex_in = x"E" else
                   "0111000" when hex_in = x"F" else
                   "1111111";

END TypeArchitecture;
